// Digital circuit NAND UNI.dig as structural Verilog
module NAND_UNI (
  input  in_1,
  input  in_2,
  input  in_3,
  input  in_4,
  input  in_5,
  input  in_6,
  input  in_7,
  input  in_8,
  input  in_9,
  input  in_10,
  input  in_11
);

  wire nand_1_out, nand_2_out, nand_3_out, nand_4_out, nand_5_out, nand_6_out, nand_7_out, nand_8_out,
       nand_9_out, nand_10_out, nand_11_out, nand_12_out, nand_13_out, nand_14_out, nand_15_out, nand_16_out,
       nand_17_out, nand_18_out, nand_19_out, nand_20_out;

  nand nand_1 (nand_1_out, in_1, in_1);
  nand nand_2 (nand_2_out, in_2, in_3);
  nand nand_3 (nand_3_out, in_4, in_4);
  nand nand_4 (nand_4_out, in_5, in_5);
  nand nand_5 (nand_5_out, in_8, in_8);
  nand nand_6 (nand_6_out, in_9, in_9);
  nand nand_7 (nand_7_out, in_6, in_6);
  nand nand_8 (nand_8_out, in_7, in_7);
  LED led_1 (.in(nand_1_out));
  nand nand_9 (nand_9_out, nand_2_out, nand_2_out);
  nand nand_10 (nand_10_out, nand_3_out, nand_4_out);
  nand nand_11 (nand_11_out, nand_5_out, nand_6_out);
  LED led_2 (.in(nand_9_out));
  nand nand_12 (nand_12_out, nand_7_out, in_7);
  nand nand_13 (nand_13_out, in_6, nand_8_out);
  LED led_3 (.in(nand_10_out));
  nand nand_14 (nand_14_out, nand_11_out, nand_11_out);
  nand nand_15 (nand_15_out, nand_12_out, nand_13_out);
  LED led_4 (.in(nand_14_out));
  nand nand_16 (nand_16_out, in_10, in_10);
  nand nand_17 (nand_17_out, in_11, in_11);
  LED led_5 (.in(nand_15_out));
  nand nand_18 (nand_18_out, nand_16_out, nand_17_out);
  nand nand_19 (nand_19_out, in_10, in_11);
  nand nand_20 (nand_20_out, nand_19_out, nand_18_out);
  LED led_6 (.in(nand_20_out));
endmodule
