// Digital circuit multiplexer.dig as structural Verilog
module multiplexer (
  input  in_1,
  input  in_2,
  input  in_3,
  input  in_4,
  input  in_5,
  input  in_6,
  input  in_7,
  input  in_8,
  input  in_9,
  input  in_10,
  input  in_11,
  output out_12,
  output out_13
);

  _74151 _74151_1 (
    .pin1(in_4), .pin2(in_5), .pin3(in_6), .pin4(in_7), .pin5(out_13), .pin6(out_12), .pin7(1'b0),
    .pin8(1'b0), .pin9(in_8), .pin10(in_9), .pin11(in_10), .pin12(in_11), .pin13(in_1), .pin14(in_2),
    .pin15(in_3), .pin16(1'b1));
endmodule
