// Digital circuit bcd to seven segment.dig as structural Verilog
module bcd_to_seven_segment (
  input  in_1,
  input  in_2,
  input  in_3,
  input  in_4,
  input  in_5,
  input  in_6,
  input  in_7
);

  wire _7447_1_pin10, _7447_1_pin11, _7447_1_pin12, _7447_1_pin13, _7447_1_pin14, _7447_1_pin15;

  _7447 _7447_1 (
    .pin1(in_2), .pin2(in_3), .pin3(in_5), .pin4(in_6), .pin5(in_7), .pin6(in_4), .pin7(in_1), .pin8(1'b0),
    .pin9(1'b1), .pin10(_7447_1_pin10), .pin11(_7447_1_pin11), .pin12(_7447_1_pin12), .pin13(_7447_1_pin13),
    .pin14(_7447_1_pin14), .pin15(_7447_1_pin15), .pin16(1'b1));
  Seven_Seg seven_seg_1 (
    .a(_7447_1_pin13), .b(_7447_1_pin12), .c(_7447_1_pin11), .d(_7447_1_pin10), .f(_7447_1_pin15),
    .g(_7447_1_pin14), .dp(1'b1));  // open: e
endmodule
