// Digital circuit demultiplexer.dig as structural Verilog
module demultiplexer (
  input  in_1,
  input  in_2,
  input  in_3,
  output out_4,
  output out_5,
  output out_6,
  output out_7,
  output out_8,
  output out_9,
  output out_10,
  output out_11,
  output out_12
);

  _74138 _74138_1 (
    .pin1(in_1), .pin2(in_2), .pin3(in_3), .pin4(1'b0), .pin5(1'b0), .pin6(1'b1), .pin7(out_4),
    .pin9(out_12), .pin10(out_11), .pin11(out_10), .pin12(out_9), .pin13(out_8), .pin14(out_7),
    .pin15(out_6), .pin16(out_5));  // open: pin8
endmodule
