// Digital circuit parallel binary adder.dig as structural Verilog
module parallel_binary_adder (
  input  in_1,
  input  in_2,
  input  in_3
);

  wire _7483_1_pin2, _7483_1_pin6, _7483_1_pin9, _7483_1_pin14, _7483_1_pin15;

  _7483 _7483_1 (
    .pin1(in_3), .pin2(_7483_1_pin2), .pin3(in_3), .pin4(in_2), .pin5(1'b1), .pin6(_7483_1_pin6),
    .pin7(in_2), .pin8(in_3), .pin9(_7483_1_pin9), .pin10(in_3), .pin11(in_2), .pin12(1'b0), .pin13(in_1),
    .pin14(_7483_1_pin14), .pin15(_7483_1_pin15), .pin16(in_2));
  LED led_1 (.in(_7483_1_pin15));
  LED led_2 (.in(_7483_1_pin2));
  LED led_3 (.in(_7483_1_pin6));
  LED led_4 (.in(_7483_1_pin9));
  LED led_5 (.in(_7483_1_pin14));
endmodule
