// Digital circuit sub.dig as structural Verilog
module sub (
  input  in_1,
  input  in_2,
  input  in_3,
  input  in_4,
  input  in_5
);

  wire and_1_out, and_2_out, and_3_out, and_4_out, not_1_out, not_2_out, not_3_out, or_1_out, xor_1_out,
       xor_2_out, xor_3_out;

  not not_1 (not_1_out, in_1);
  not not_2 (not_2_out, in_1);
  not not_3 (not_3_out, in_4);
  xor xor_1 (xor_1_out, in_1, in_2);
  xor xor_2 (xor_2_out, in_4, in_5);
  and and_1 (and_1_out, not_3_out, in_5);
  and and_2 (and_2_out, not_1_out, in_2);
  and and_3 (and_3_out, not_2_out, in_3);
  and and_4 (and_4_out, in_2, in_3);
  LED led_1 (.in(xor_2_out));
  LED led_2 (.in(and_1_out));
  xor xor_3 (xor_3_out, xor_1_out, in_3);
  or or_1 (or_1_out, and_2_out, and_3_out, and_4_out);
  LED led_3 (.in(xor_3_out));
  LED led_4 (.in(or_1_out));
endmodule
